// Logisim project 4bit-adder.circ as structural Verilog: 2 circuits, main circuit main
module main (
  input  Constant_In,
  input  A,
  input  B,
  output out_4,
  output out_5
);

  wire and_1_out, and_2_out, xor_1_out;

  xor xor_1 (xor_1_out, A, B);
  and and_1 (and_1_out, A, B);
  xor xor_2 (out_4, Constant_In, xor_1_out);
  and and_2 (and_2_out, Constant_In, xor_1_out);
  or or_1 (out_5, and_2_out, and_1_out);
endmodule

module fa (
  input  [3:0] A,
  input  [3:0] B,
  output [3:0] Sum,
  output out_4
);

  wire main_1_out_5, main_2_out_5, main_3_out_5;

  main main_1 (.Constant_In(1'b0), .A(A[0]), .B(B[0]), .out_4(Sum[0]), .out_5(main_1_out_5));
  main main_2 (.Constant_In(main_1_out_5), .A(A[1]), .B(B[1]), .out_4(Sum[1]), .out_5(main_2_out_5));
  main main_3 (.Constant_In(main_2_out_5), .A(A[2]), .B(B[2]), .out_4(Sum[2]), .out_5(main_3_out_5));
  main main_4 (.Constant_In(main_3_out_5), .A(A[3]), .B(B[3]), .out_4(Sum[3]), .out_5(out_4));

  // Notes on the sheet:
  //   Constant in
endmodule
